# Fritzing sketch tkpower (saved by Fritzing 0.9.2b)
circuit board: 8.46667cm x 5.64444cm
breadboards: 1

parts:
  Part1 = Pro Trinket 5V
  R1 = Resistor [tolerance=±5% resistance=33 package=THT]
  C1 = Electrolytic Capacitor [capacitance=1µF package="100 mil [THT, electrolytic]"]
  J4 = Screw terminal - 2 pins [package=THT]
  R3 = Resistor [tolerance=±5% resistance=1M package=THT]
  R2 = Resistor [tolerance=±5% resistance=1M package=THT]

nets:
  5V: Part1.VBAT, R2.Pin_0
  GND: Part1.GND, C1.-, R3.Pin_1
  N1: Part1.A0, R1.Pin_1, J4.pin2
  N2: R1.Pin_0, C1.+, J4.pin1, R3.Pin_0, R2.Pin_1

notes:
  Current Clamp connects to J4

custom parts:
  Pro Trinket 5V: The Pro Trinket 5V is like an Arduino Pro Mini with more pins and USB included. Built with the common core Arduino chip, the ATmega328p, it has 18 GPIO, 2 extra analog inputs, 28K of flash, and 2K of RAM. It has onboard USB bootloading support with Optiboot support, so you can either program your Pro Trinket over USB or with a FTDI cable. The Pro Trinket is programmable using the Arduino IDE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
